# Fritzing sketch SSD1306_Wiring_Final (saved by Fritzing 0.9.3b)
circuit board: 2.69072cm x 5.52472cm

parts:
  J1 = female pin header, 8 pins [form="♀ (female)"]
  Raspberry_Pi3_B+ = Raspberry Pi B+

nets:
  N1: J1.pin1, Raspberry_Pi3_B+.GPIO2
  N2: J1.pin2, Raspberry_Pi3_B+.GPIO3
  N3: J1.pin4, Raspberry_Pi3_B+.GPIO24
  N4: J1.pin7, Raspberry_Pi3_B+.3v3
  N5: J1.pin8, Raspberry_Pi3_B+.GND

notes:
  3.3v
  SDA
  SCL
  GND
  RST
