# Fritzing sketch SSD1306_Wiring_Final (saved by Fritzing 0.9.3b)
circuit board: 2.69072cm x 5.52472cm
breadboards: 1

parts:
  Raspberry_Pi3_B+ = Raspberry Pi B+
  Part2 = OLED Monochrome 128x64 1.3 inch [part_number=938]

nets:
  3V3: Raspberry_Pi3_B+.3v3, Raspberry_Pi3_B+.3V3, Part2.VIN
  N1: Raspberry_Pi3_B+.GPIO2, Part2.MOSI_SDA
  N2: Raspberry_Pi3_B+.GPIO3, Part2.SCLK_SCK
  GND: Raspberry_Pi3_B+.GND, Part2.GND
  N3: Raspberry_Pi3_B+.GPIO24, Part2.RESET

notes:
  3.3v
  SDA
  SCL
  GND
  RST

custom parts:
  OLED Monochrome 128x64 1.3 inch: These displays are small, only about 1.3" diagonal, but very readable due to the high contrast of an OLED display. This display is made of 128x64 individual white OLED pixels, each one is turned on or off by the controller chip. Because the display makes its own light, no backlight is required. This reduces the power required to run the OLED and is why the display has such high contrast; we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
